// Logisim project guess_your_number.circ as structural Verilog: 7 circuits, main circuit main
module main (
);

  wire CLK, display_1_a1, display_1_a2, display_1_b1, display_1_b2, display_1_c1, display_1_c2, display_1_d1,
       display_1_d2, display_1_e1, display_1_e2, display_1_f1, display_1_f2, display_1_g1, display_1_g2,
       displaywrapper_1_canselect, displaywrapper_1_reset_2, displaywrapper_1_resetheader,
       displaywrapper_1_resettable, displaywrapper_1_writeheader, displaywrapper_1_writetable, N_out, RESET,
       START, thinker_1_writethinker, Y_out;
  wire [2:0] thinker_1_state;
  wire [5:0] thinker_1_guess;
  wire [6:0] displaywrapper_1_data1, displaywrapper_1_data2;

  Clock clock_1 (.out(CLK));
  Button button_1 (.out(START));
  Button button_2 (.out(RESET));
  DisplayWrapper displaywrapper_1 (
    .Reset(RESET), .ResetHeader(displaywrapper_1_resetheader), .WriteHeader(displaywrapper_1_writeheader),
    .WriteTable(displaywrapper_1_writetable), .CLK(CLK), .ResetTable(displaywrapper_1_resettable),
    .Data1(displaywrapper_1_data1), .Data2(displaywrapper_1_data2), .WriteThinker(thinker_1_writethinker),
    .Start(START), .State(thinker_1_state), .Reset_2(displaywrapper_1_reset_2),
    .CanSelect(displaywrapper_1_canselect));
  TTY #(.rows(1)) tty_1 (
    .data(displaywrapper_1_data1), .clk(displaywrapper_1_writeheader), .clr(displaywrapper_1_resetheader));  // open: we
  TTY #(.rows(4), .cols(30)) tty_2 (
    .data(displaywrapper_1_data2), .clk(displaywrapper_1_writetable), .clr(displaywrapper_1_resettable));  // open: we
  Button Y (.out(Y_out));
  Button N (.out(N_out));
  _7_Segment_Display u_7_segment_display_1 (
    .g(display_1_a1), .f(display_1_b1), .a(display_1_c1), .b(display_1_d1), .e(display_1_e1),
    .d(display_1_f1), .c(display_1_g1));  // open: dp
  Display display_1 (
    .Data(thinker_1_guess), .a1(display_1_a1), .b1(display_1_b1), .c1(display_1_c1), .d1(display_1_d1),
    .e1(display_1_e1), .f1(display_1_f1), .g1(display_1_g1), .a2(display_1_a2), .b2(display_1_b2),
    .c2(display_1_c2), .d2(display_1_d2), .e2(display_1_e2), .f2(display_1_f2), .g2(display_1_g2));
  Thinker thinker_1 (
    .Yes(Y_out), .No(N_out), .CanSelect(displaywrapper_1_canselect), .CLK(CLK), .State(thinker_1_state),
    .Reset(displaywrapper_1_reset_2), .WriteThinker(thinker_1_writethinker), .Guess(thinker_1_guess));
  _7_Segment_Display u_7_segment_display_2 (
    .g(display_1_a2), .f(display_1_b2), .a(display_1_c2), .b(display_1_d2), .e(display_1_e2),
    .d(display_1_f2), .c(display_1_g2));  // open: dp

  // Notes on the sheet:
  //   How to play:
  //   Configuration:
  //   1. Pick a number from 1 to 63
  //   2. Click 'Start' to start the game
  //   4. If You want to play again, click 'Reset'
  //   3. Answer the questions by clicking 'Y' or 'N'
  //   For the correct use of the game, you must set the Tick Frequency (Clock) to 128Hz-256Hz and zoom to 200%
endmodule

module TTYLogic (
  input  Reset,
  input  CLK,
  input  Start,
  input  [2:0] Sel,
  output [9:0] ADDR,
  output ResetHeader,
  output WriteH,
  output CAN_SELECT,
  output WriteTBL
);

  wire and_1_out, comparator_1_eq, comparator_2_eq, comparator_2_gt, comparator_3_eq, or_1_out, or_3_out;
  wire [9:0] multiplexer_1_out;

  Counter #(.width(10), .max('h28e), .ongoal("stay")) counter_1 (
    .Q(ADDR), .clk(or_1_out), .clr(Reset));  // open: load, D, count, carry
  or or_1 (or_1_out, WriteH, WriteTBL, ResetHeader);
  or or_2 (ResetHeader, comparator_3_eq, and_1_out);
  and and_1 (and_1_out, Start, comparator_1_eq);
  Multiplexer #(.select(3), .width(10)) multiplexer_1 (
    .in0(10'h93), .in1(10'hf3), .in2(10'h15c), .in3(10'h1bc), .in4(10'h21c), .in5(10'h27c), .in6(10'h28e),
    .out(multiplexer_1_out), .sel(Sel));  // open: in7, en
  Comparator #(.width(10), .mode("unsigned")) comparator_1 (
    .a(ADDR), .b(10'h1a), .eq(comparator_1_eq));  // open: gt, lt
  Comparator #(.width(10), .mode("unsigned")) comparator_2 (
    .a(ADDR), .b(10'h33), .gt(comparator_2_gt), .eq(comparator_2_eq));  // open: lt
  Comparator #(.width(10), .mode("unsigned")) comparator_3 (
    .a(ADDR), .b(10'h28e), .eq(comparator_3_eq));  // open: gt, lt
  Comparator #(.width(10), .mode("unsigned")) comparator_4 (
    .a(ADDR), .b(multiplexer_1_out), .eq(CAN_SELECT));  // open: gt, lt
  and and_2 (WriteH, ~comparator_1_eq, ~comparator_2_eq, ~comparator_2_gt, CLK);  // AND_Gate
  or or_3 (or_3_out, comparator_2_eq, comparator_2_gt);
  and and_3 (WriteTBL, or_3_out, CLK, ~CAN_SELECT);  // AND_Gate

  // Other names for the same wires on the sheet: WH = WriteH; WTBL = WriteTBL
endmodule

// 7SD
module _7SegDriver (
  input  b3,
  input  b2,
  input  b1,
  input  b0,
  output a,
  output b,
  output c,
  output d,
  output e,
  output f,
  output g
);

  wire and_1_out, and_2_out, and_3_out, and_4_out, and_5_out, and_6_out, and_7_out, and_8_out, and_9_out,
       and_10_out, and_11_out, and_12_out, and_13_out, and_14_out, and_15_out, and_16_out, not_1_out,
       not_2_out, not_3_out, not_4_out, not_5_out, not_6_out, not_7_out, not_8_out, not_9_out, not_10_out,
       not_11_out, not_12_out, not_13_out, not_14_out, not_15_out, not_16_out, not_17_out, not_18_out,
       not_19_out, not_20_out, not_21_out;

  not not_1 (not_1_out, b2);
  and and_1 (and_1_out, not_1_out, b1);
  and and_2 (and_2_out, b2, not_2_out);
  not not_2 (not_2_out, b1);
  and and_3 (and_3_out, b2, not_3_out);
  not not_3 (not_3_out, b0);
  not not_4 (not_4_out, b1);
  and and_4 (and_4_out, not_4_out, not_5_out);
  not not_5 (not_5_out, b0);
  and and_5 (and_5_out, b2, not_6_out);
  not not_6 (not_6_out, b1);
  and and_6 (and_6_out, b2, not_7_out);
  not not_7 (not_7_out, b0);
  not not_8 (not_8_out, b2);
  and and_7 (and_7_out, not_8_out, not_9_out);
  not not_9 (not_9_out, b0);
  and and_8 (and_8_out, b2, b0);
  not not_10 (not_10_out, b2);
  not not_11 (not_11_out, b1);
  and and_9 (and_9_out, not_11_out, not_12_out);
  not not_12 (not_12_out, b0);
  and and_10 (and_10_out, b1, b0);
  not not_13 (not_13_out, b2);
  and and_11 (and_11_out, not_13_out, not_14_out);
  not not_14 (not_14_out, b0);
  and and_12 (and_12_out, b1, not_15_out);
  not not_15 (not_15_out, b0);
  not not_16 (not_16_out, b2);
  and and_13 (and_13_out, not_16_out, not_17_out);
  not not_17 (not_17_out, b0);
  not not_18 (not_18_out, b2);
  and and_14 (and_14_out, not_18_out, b1);
  and and_15 (and_15_out, b1, not_19_out);
  not not_19 (not_19_out, b0);
  and and_16 (and_16_out, b2, not_20_out, b0);
  not not_20 (not_20_out, b1);
  not not_21 (not_21_out, b1);
  or or_1 (g, not_21_out, b0, b2);
  or or_2 (a, and_1_out, and_2_out, and_3_out, b3);
  or or_3 (b, and_4_out, and_5_out, and_6_out, b3);
  or or_4 (c, and_7_out, b1, and_8_out, b3);
  or or_5 (d, not_10_out, and_9_out, and_10_out);
  or or_6 (e, and_11_out, and_12_out);
  or or_7 (f, and_13_out, and_14_out, and_15_out, and_16_out, b3);
endmodule

// BTBCD
module BinToBCD (
  input  b5,
  input  b4,
  input  b3,
  input  b2,
  input  b1,
  input  b0,
  output a,
  output b,
  output c,
  output d,
  output e,
  output f,
  output g,
  output h
);

  wire and_1_out, and_2_out, and_3_out, and_4_out, and_5_out, and_6_out, and_7_out, and_8_out, and_9_out,
       and_10_out, and_11_out, and_12_out, and_13_out, and_14_out, and_15_out, and_16_out, and_17_out,
       and_18_out, and_19_out, and_20_out, and_21_out, and_22_out, and_23_out, and_24_out, and_25_out,
       and_26_out, and_27_out, and_28_out, and_29_out, and_30_out, and_31_out, and_32_out, and_33_out,
       and_34_out, and_35_out, and_36_out, and_37_out, and_38_out, not_1_out, not_2_out, not_3_out,
       not_4_out, not_5_out, not_6_out, not_7_out, not_8_out, not_9_out, not_10_out, not_11_out, not_12_out,
       not_13_out, not_14_out, not_15_out, not_16_out, not_17_out, not_18_out, not_19_out, not_20_out,
       not_21_out, not_22_out, not_23_out, not_24_out, not_25_out, not_26_out, not_27_out, not_28_out,
       not_29_out, not_30_out, not_31_out, not_32_out, not_33_out, not_34_out, not_35_out, not_36_out,
       not_37_out, not_38_out, not_39_out, not_40_out, not_41_out, not_42_out, not_43_out, not_44_out,
       not_45_out, not_46_out, not_47_out, not_48_out, not_49_out, not_50_out, not_51_out, not_52_out,
       not_53_out, not_54_out, not_55_out, not_56_out, not_57_out, not_58_out, not_59_out, not_60_out,
       not_61_out, not_62_out, not_63_out, not_64_out, not_65_out, not_66_out, not_67_out, not_68_out,
       not_69_out, not_70_out, not_71_out;

  and and_1 (and_1_out, b5, b3);
  and and_2 (and_2_out, b5, b4);
  not not_1 (not_1_out, b5);
  not not_2 (not_2_out, b5);
  not not_3 (not_3_out, b4);
  not not_4 (not_4_out, b3);
  not not_5 (not_5_out, b5);
  not not_6 (not_6_out, b4);
  not not_7 (not_7_out, b5);
  not not_8 (not_8_out, b4);
  not not_9 (not_9_out, b5);
  not not_10 (not_10_out, b5);
  not not_11 (not_11_out, b3);
  not not_12 (not_12_out, b2);
  not not_13 (not_13_out, b4);
  not not_14 (not_14_out, b3);
  not not_15 (not_15_out, b3);
  not not_16 (not_16_out, b3);
  not not_17 (not_17_out, b2);
  not not_18 (not_18_out, b5);
  not not_19 (not_19_out, b4);
  not not_20 (not_20_out, b2);
  not not_21 (not_21_out, b1);
  not not_22 (not_22_out, b5);
  not not_23 (not_23_out, b3);
  not not_24 (not_24_out, b2);
  not not_25 (not_25_out, b5);
  not not_26 (not_26_out, b1);
  not not_27 (not_27_out, b4);
  not not_28 (not_28_out, b3);
  not not_29 (not_29_out, b3);
  not not_30 (not_30_out, b2);
  not not_31 (not_31_out, b1);
  not not_32 (not_32_out, b2);
  not not_33 (not_33_out, b4);
  not not_34 (not_34_out, b3);
  not not_35 (not_35_out, b1);
  not not_36 (not_36_out, b5);
  not not_37 (not_37_out, b4);
  not not_38 (not_38_out, b5);
  not not_39 (not_39_out, b2);
  not not_40 (not_40_out, b1);
  not not_41 (not_41_out, b5);
  not not_42 (not_42_out, b2);
  not not_43 (not_43_out, b2);
  not not_44 (not_44_out, b1);
  not not_45 (not_45_out, b4);
  not not_46 (not_46_out, b3);
  not not_47 (not_47_out, b2);
  not not_48 (not_48_out, b4);
  not not_49 (not_49_out, b3);
  not not_50 (not_50_out, b5);
  not not_51 (not_51_out, b4);
  not not_52 (not_52_out, b3);
  not not_53 (not_53_out, b5);
  not not_54 (not_54_out, b3);
  not not_55 (not_55_out, b5);
  not not_56 (not_56_out, b4);
  not not_57 (not_57_out, b1);
  not not_58 (not_58_out, b5);
  not not_59 (not_59_out, b3);
  not not_60 (not_60_out, b2);
  not not_61 (not_61_out, b1);
  not not_62 (not_62_out, b5);
  not not_63 (not_63_out, b2);
  not not_64 (not_64_out, b4);
  not not_65 (not_65_out, b3);
  not not_66 (not_66_out, b1);
  not not_67 (not_67_out, b3);
  not not_68 (not_68_out, b1);
  not not_69 (not_69_out, b4);
  not not_70 (not_70_out, b2);
  not not_71 (not_71_out, b1);
  or or_1 (b, and_1_out, and_2_out);
  and and_3 (and_3_out, not_1_out, b4, b2);
  and and_4 (and_4_out, not_2_out, b4, b3);
  and and_5 (and_5_out, b4, b3, b2);
  and and_6 (and_6_out, b5, not_3_out, not_4_out);
  and and_7 (and_7_out, not_5_out, not_6_out, b3, b1);
  and and_8 (and_8_out, not_7_out, not_8_out, b3, b2);
  and and_9 (and_9_out, not_9_out, b3, b2, b1);
  and and_10 (and_10_out, not_10_out, b4, not_11_out, not_12_out);
  and and_11 (and_11_out, b5, not_13_out, not_14_out);
  and and_12 (and_12_out, b5, not_15_out, b1);
  and and_13 (and_13_out, b5, not_16_out, b2);
  and and_14 (and_14_out, b5, b4, b3, not_17_out);
  and and_15 (and_15_out, not_18_out, not_19_out, b3, not_20_out, not_21_out);
  and and_16 (and_16_out, not_22_out, b4, not_23_out, not_24_out, b1);
  and and_17 (and_17_out, not_25_out, b4, b3, b2, not_26_out);
  and and_18 (and_18_out, b5, not_27_out, not_28_out, b2, b1);
  and and_19 (and_19_out, b5, b4, not_29_out, not_30_out, not_31_out);
  and and_20 (and_20_out, b5, b4, b3, not_32_out, b1);
  and and_21 (and_21_out, not_33_out, not_34_out, b2, not_35_out);
  and and_22 (and_22_out, not_36_out, not_37_out, b2, b1);
  and and_23 (and_23_out, not_38_out, b4, not_39_out, not_40_out);
  and and_24 (and_24_out, not_41_out, b4, b3, not_42_out);
  and and_25 (and_25_out, b4, b3, not_43_out, not_44_out);
  and and_26 (and_26_out, b5, not_45_out, not_46_out, not_47_out, b1);
  and and_27 (and_27_out, b5, not_48_out, b3, b2);
  and and_28 (and_28_out, b5, b4, not_49_out, b2, b1);
  and and_29 (and_29_out, not_50_out, not_51_out, not_52_out, b1);
  and and_30 (and_30_out, not_53_out, not_54_out, b2, b1);
  and and_31 (and_31_out, not_55_out, not_56_out, b3, b2, not_57_out);
  and and_32 (and_32_out, not_58_out, b4, not_59_out, not_60_out, not_61_out);
  and and_33 (and_33_out, not_62_out, b4, b3, not_63_out, b1);
  and and_34 (and_34_out, b5, not_64_out, not_65_out, not_66_out);
  and and_35 (and_35_out, b5, not_67_out, b2, not_68_out);
  and and_36 (and_36_out, b5, not_69_out, b3, b1);
  and and_37 (and_37_out, b5, b3, b2, b1);
  and and_38 (and_38_out, b5, b4, b3, not_70_out, not_71_out);
  or or_2 (c, and_3_out, and_4_out, and_5_out, and_6_out);
  or or_3 (d, and_7_out, and_8_out, and_9_out, and_10_out, and_11_out, and_12_out, and_13_out, and_14_out);
  or or_4 (e, and_15_out, and_16_out, and_17_out, and_18_out, and_19_out, and_20_out);
  or or_5 (f, and_21_out, and_22_out, and_23_out, and_24_out, and_25_out, and_26_out, and_27_out, and_28_out);
  or or_6 (g, and_29_out, and_30_out, and_31_out, and_32_out, and_33_out, and_34_out, and_35_out, and_36_out, and_37_out, and_38_out);

  assign a = 1'b0;
  assign h = b0;
endmodule

module Display (
  input  [5:0] Data,
  output a1,
  output b1,
  output c1,
  output d1,
  output e1,
  output f1,
  output g1,
  output a2,
  output b2,
  output c2,
  output d2,
  output e2,
  output f2,
  output g2
);

  wire bintobcd_1_a, bintobcd_1_b, bintobcd_1_c, bintobcd_1_d, bintobcd_1_e, bintobcd_1_f, bintobcd_1_g,
       bintobcd_1_h;

  BinToBCD bintobcd_1 (
    .b5(Data[5]), .b4(Data[4]), .b3(Data[3]), .b2(Data[2]), .b1(Data[1]), .b0(Data[0]), .a(bintobcd_1_a),
    .b(bintobcd_1_b), .c(bintobcd_1_c), .d(bintobcd_1_d), .e(bintobcd_1_e), .f(bintobcd_1_f),
    .g(bintobcd_1_g), .h(bintobcd_1_h));
  _7SegDriver u_7segdriver_1 (
    .b3(bintobcd_1_a), .b2(bintobcd_1_b), .b1(bintobcd_1_c), .b0(bintobcd_1_d), .a(a1), .b(b1), .c(c1),
    .d(d1), .e(e1), .f(f1), .g(g1));
  _7SegDriver u_7segdriver_2 (
    .b3(bintobcd_1_e), .b2(bintobcd_1_f), .b1(bintobcd_1_g), .b0(bintobcd_1_h), .a(a2), .b(b2), .c(c2),
    .d(d2), .e(e2), .f(f2), .g(g2));
endmodule

module Thinker (
  input  Reset,
  input  Yes,
  input  No,
  input  CanSelect,
  input  CLK,
  output [5:0] Guess,
  output [2:0] State,
  output WriteThinker
);

  wire and_2_out, or_1_out;
  wire [5:0] d_ff_6_q;

  Counter #(.width(3), .max('h6)) counter_1 (
    .count(WriteThinker), .Q(State), .clk(CLK), .clr(Reset));  // open: load, D, carry
  or or_1 (or_1_out, Yes, No);
  and and_1 (WriteThinker, or_1_out, CanSelect);
  and and_2 (and_2_out, Yes, 1'b1);
  D_Flip_Flop d_ff_1 (.clk(CLK), .D(and_2_out), .Q(d_ff_6_q[5]), .en(WriteThinker), .reset(Reset));  // open: Qn, preset
  Demultiplexer #(.select(3), .width(6)) demultiplexer_1 (
    .out6(Guess), .in(d_ff_6_q), .sel(State));  // open: out0, out1, out2, out3, out4, out5, out7, en
  D_Flip_Flop d_ff_2 (
    .clk(CLK), .D(d_ff_6_q[5]), .Q(d_ff_6_q[4]), .en(WriteThinker), .reset(Reset));  // open: Qn, preset
  D_Flip_Flop d_ff_3 (
    .clk(CLK), .D(d_ff_6_q[4]), .Q(d_ff_6_q[3]), .en(WriteThinker), .reset(Reset));  // open: Qn, preset
  D_Flip_Flop d_ff_4 (
    .clk(CLK), .D(d_ff_6_q[3]), .Q(d_ff_6_q[2]), .en(WriteThinker), .reset(Reset));  // open: Qn, preset
  D_Flip_Flop d_ff_5 (
    .clk(CLK), .D(d_ff_6_q[2]), .Q(d_ff_6_q[1]), .en(WriteThinker), .reset(Reset));  // open: Qn, preset
  D_Flip_Flop d_ff_6 (
    .clk(CLK), .D(d_ff_6_q[1]), .Q(d_ff_6_q[0]), .en(WriteThinker), .reset(Reset));  // open: Qn, preset

  // Other names for the same wires on the sheet: WT = WriteThinker
endmodule

module DisplayWrapper (
  input  CLK,
  input  Reset,
  input  Start,
  input  [2:0] State,
  input  WriteThinker,
  output Reset_2,
  output CanSelect,
  output [6:0] Data1,
  output [6:0] Data2,
  output WriteHeader,
  output WriteTable,
  output ResetHeader,
  output ResetTable
);

  wire R_HEAD;
  wire [9:0] ttylogic_1_addr;

  or or_1 (ResetHeader, R_HEAD, Reset);
  or or_2 (ResetTable, WriteThinker, Reset);
  TTYLogic ttylogic_1 (
    .ResetHeader(R_HEAD), .Start(Start), .ADDR(ttylogic_1_addr), .Reset(Reset), .WriteH(WriteHeader),
    .CLK(CLK), .WriteTBL(WriteTable), .Sel(State), .CAN_SELECT(CanSelect));
  ROM #(.addrWidth(10), .dataWidth(7)) rom_1 (.addr(ttylogic_1_addr), .data(Data1));  // open: sel

  assign Data2 = Data1;
  assign Reset_2 = Reset;

  // Other names for the same wires on the sheet: CAN_S = CanSelect

  // Notes on the sheet:
  //   contents of rom_1 (hex, n*v repeats v):
  //   50 69 63 6b 20 61 20 6e 75 6d 62 65 72 20 66 72 6f 6d 20 31 20 74 6f 20 36 33 0 0 44 6f 20 79 6f 75
  //   20 73 65 65 20 79 6f 75 72 20 6e 75 6d 62 65 72 3f 0 30 31 20 30 33 20 30 35 20 30 37 20 30 39 20 31
  //   31 20 31 33 20 31 35 20 31 37 20 31 39 20 32 31 20 32 33 20 32 35 20 32 37 20 32 39 20 33 31 20 33
  //   33 20 33 35 20 33 37 20 33 39 20 34 31 20 34 33 20 34 35 20 34 37 20 34 39 20 35 31 20 35 33 20 35
  //   35 20 35 37 20 35 39 20 36 31 20 36 33 0 30 32 20 30 33 20 30 36 20 30 37 20 31 30 20 31 31 20 31 34
  //   20 31 35 20 31 38 20 31 39 20 32 32 20 32 33 20 32 36 20 32 37 20 33 30 20 33 31 20 33 34 20 33 35
  //   20 33 38 20 33 39 20 34 32 20 34 33 20 34 36 20 34 37 20 35 30 20 35 31 20 35 34 20 35 35 20 35 38
  //   20 35 39 20 36 32 20 36 33 0 30 34 20 30 35 20 30 36 20 30 37 20 31 32 20 31 32 20 31 33 20 31 34 20
  //   31 35 20 32 30 20 32 31 20 32 32 20 32 33 20 32 38 20 32 39 20 33 30 20 33 31 20 33 36 20 33 37 20
  //   33 38 20 33 39 20 34 34 20 34 35 20 34 35 20 34 36 20 34 36 20 34 37 20 35 32 20 35 33 20 35 34 20
  //   35 35 20 36 30 20 36 31 20 36 32 20 36 33 0 30 38 20 30 39 20 31 30 20 31 31 20 31 32 20 31 33 20 31
  //   34 20 31 35 20 32 34 20 32 35 20 32 36 20 32 37 20 32 38 20 32 39 20 33 30 20 33 31 20 34 30 20 34
  //   31 20 34 32 20 34 33 20 34 34 20 34 35 20 34 36 20 34 37 20 35 36 20 35 37 20 35 38 20 35 39 20 36
  //   30 20 36 31 20 36 32 20 36 33 0 31 36 20 31 37 20 31 38 20 31 39 20 32 30 20 32 31 20 32 32 20 32 33
  //   20 32 34 20 32 35 20 32 36 20 32 37 20 32 38 20 32 39 20 33 30 20 33 31 20 34 38 20 34 39 20 35 30
  //   20 35 31 20 35 32 20 35 33 20 35 34 20 35 35 20 35 36 20 35 37 20 35 38 20 35 39 20 36 30 20 36 31
  //   20 36 32 20 36 33 0 33 32 20 33 33 20 33 34 20 33 35 20 33 36 20 33 37 20 33 38 20 33 39 20 34 30 20
  //   34 31 20 34 32 20 34 33 20 34 34 20 34 35 20 34 36 20 34 37 20 34 38 20 34 39 20 35 30 20 35 31 20
  //   35 32 20 35 33 20 35 34 20 35 35 20 35 36 20 35 37 20 35 38 20 35 39 20 36 30 20 36 31 20 36 32 20
  //   36 33 0 59 6f 75 72 20 6e 75 6d 62 65 72 20 69 73 2e 2e 2e
endmodule
